// Logisim project riscv_simulator.circ as structural Verilog: 1 circuit, main circuit main
module main (
  input  in_1,
  input  [1:0] in_2,
  input  in_3,
  input  [1:0] in_4,
  output [31:0] out_5
);

  wire clock_2_out, clock_3_out, GatePC, LD_PC, not_1_out, or_1_out;
  wire [4:0] multiplexer_3_out;
  wire [7:0] decoder_2_out0, decoder_2_out8, decoder_2_out16, decoder_2_out24, decoder_3_out0,
       decoder_3_out8, decoder_3_out16, decoder_3_out24;
  wire [31:0] adder_1_out, controlled_buffer_1_out, multiplexer_1_out, multiplexer_2_out, x1_q, x2_q, x3_q,
       x4_q, x5_q, x6_q, x7_q, x8_q, x9_q, x10_q, x11_q, x12_q, x13_q, x14_q, x15_q, x16_q, x17_q, x18_q,
       x19_q, x20_q, x21_q, x22_q, x23_q, x24_q, x25_q, x26_q, x27_q, x28_q, x29_q, x30_q, x31_q;
  wire [31:1] decoder_1_out1;

  Clock clock_1 ();  // open: out
  not not_1 (not_1_out, in_1);
  Multiplexer #(.width(32)) multiplexer_1 (
    .in0(32'hdeadbeef), .in1(multiplexer_2_out), .out(multiplexer_1_out), .sel(not_1_out));
  or or_1 (or_1_out, in_1, LD_PC);
  Clock clock_2 (.out(clock_2_out));
  Multiplexer #(.select(2), .width(32)) multiplexer_2 (
    .in0(adder_1_out), .in1(32'hdeadbeef), .in2(32'hdeadbeef), .in3(32'hdeadbeef), .out(multiplexer_2_out),
    .sel(in_2));
  Register #(.width(32)) PC (.D(multiplexer_1_out), .en(or_1_out), .clk(clock_2_out), .Q(out_5));  // open: clr
  Adder #(.width(32)) adder_1 (.a(32'h4), .b(out_5), .out(adder_1_out));  // open: cin, cout
  assign controlled_buffer_1_out = GatePC ? out_5 : 32'bz;  // Controlled_Buffer controlled_buffer_1
  Decoder #(.select(5)) decoder_1 (
    .out1(decoder_1_out1[1]), .out2(decoder_1_out1[2]), .out3(decoder_1_out1[3]), .out4(decoder_1_out1[4]),
    .out5(decoder_1_out1[5]), .out6(decoder_1_out1[6]), .out7(decoder_1_out1[7]), .out8(decoder_1_out1[8]),
    .out9(decoder_1_out1[9]), .out10(decoder_1_out1[10]), .out11(decoder_1_out1[11]),
    .out12(decoder_1_out1[12]), .out13(decoder_1_out1[13]), .out14(decoder_1_out1[14]),
    .out15(decoder_1_out1[15]), .out16(decoder_1_out1[16]), .out17(decoder_1_out1[17]),
    .out18(decoder_1_out1[18]), .out19(decoder_1_out1[19]), .out20(decoder_1_out1[20]),
    .out21(decoder_1_out1[21]), .out22(decoder_1_out1[22]), .out23(decoder_1_out1[23]),
    .out24(decoder_1_out1[24]), .out25(decoder_1_out1[25]), .out26(decoder_1_out1[26]),
    .out27(decoder_1_out1[27]), .out28(decoder_1_out1[28]), .out29(decoder_1_out1[29]),
    .out30(decoder_1_out1[30]), .out31(decoder_1_out1[31]), .sel(multiplexer_3_out), .en(in_3));  // open: out0
  Multiplexer #(.select(2), .width(5)) multiplexer_3 (
    .in0({5{1'b0}}), .in1(5'b01000), .in2(5'b10000), .in3(5'b11000), .out(multiplexer_3_out));  // open: sel
  Decoder #(.select(5)) decoder_2 (
    .out0(decoder_2_out0[0]), .out1(decoder_2_out0[1]), .out2(decoder_2_out0[2]), .out3(decoder_2_out0[3]),
    .out4(decoder_2_out0[4]), .out5(decoder_2_out0[5]), .out6(decoder_2_out0[6]), .out7(decoder_2_out0[7]),
    .out8(decoder_2_out8[0]), .out9(decoder_2_out8[1]), .out10(decoder_2_out8[2]), .out11(decoder_2_out8[3]),
    .out12(decoder_2_out8[4]), .out13(decoder_2_out8[5]), .out14(decoder_2_out8[6]),
    .out15(decoder_2_out8[7]), .out16(decoder_2_out16[0]), .out17(decoder_2_out16[1]),
    .out18(decoder_2_out16[2]), .out19(decoder_2_out16[3]), .out20(decoder_2_out16[4]),
    .out21(decoder_2_out16[5]), .out22(decoder_2_out16[6]), .out23(decoder_2_out16[7]),
    .out24(decoder_2_out24[0]), .out25(decoder_2_out24[1]), .out26(decoder_2_out24[2]),
    .out27(decoder_2_out24[3]), .out28(decoder_2_out24[4]), .out29(decoder_2_out24[5]),
    .out30(decoder_2_out24[6]), .out31(decoder_2_out24[7]));  // open: sel, en
  Clock clock_3 (.out(clock_3_out));
  Register #(.width(32)) x1 (.D(32'hdeadbeef), .en(decoder_1_out1[1]), .clk(clock_3_out), .Q(x1_q));  // open: clr
  Register #(.width(32)) x2 (.D(32'hdeadbeef), .en(decoder_1_out1[2]), .clk(clock_3_out), .Q(x2_q));  // open: clr
  Register #(.width(32)) x3 (.D(32'hdeadbeef), .en(decoder_1_out1[3]), .clk(clock_3_out), .Q(x3_q));  // open: clr
  Register #(.width(32)) x4 (.D(32'hdeadbeef), .en(decoder_1_out1[4]), .clk(clock_3_out), .Q(x4_q));  // open: clr
  Register #(.width(32)) x5 (.D(32'hdeadbeef), .en(decoder_1_out1[5]), .clk(clock_3_out), .Q(x5_q));  // open: clr
  Register #(.width(32)) x6 (.D(32'hdeadbeef), .en(decoder_1_out1[6]), .clk(clock_3_out), .Q(x6_q));  // open: clr
  Register #(.width(32)) x7 (.D(32'hdeadbeef), .en(decoder_1_out1[7]), .clk(clock_3_out), .Q(x7_q));  // open: clr
  Register #(.width(32)) x8 (.D(32'hdeadbeef), .en(decoder_1_out1[8]), .clk(clock_3_out), .Q(x8_q));  // open: clr
  Register #(.width(32)) x9 (.D(32'hdeadbeef), .en(decoder_1_out1[9]), .clk(clock_3_out), .Q(x9_q));  // open: clr
  Register #(.width(32)) x10 (.D(32'hdeadbeef), .en(decoder_1_out1[10]), .clk(clock_3_out), .Q(x10_q));  // open: clr
  Register #(.width(32)) x11 (.D(32'hdeadbeef), .en(decoder_1_out1[11]), .clk(clock_3_out), .Q(x11_q));  // open: clr
  Register #(.width(32)) x12 (.D(32'hdeadbeef), .en(decoder_1_out1[12]), .clk(clock_3_out), .Q(x12_q));  // open: clr
  Register #(.width(32)) x13 (.D(32'hdeadbeef), .en(decoder_1_out1[13]), .clk(clock_3_out), .Q(x13_q));  // open: clr
  Register #(.width(32)) x14 (.D(32'hdeadbeef), .en(decoder_1_out1[14]), .clk(clock_3_out), .Q(x14_q));  // open: clr
  Register #(.width(32)) x15 (.D(32'hdeadbeef), .en(decoder_1_out1[15]), .clk(clock_3_out), .Q(x15_q));  // open: clr
  Decoder #(.select(5)) decoder_3 (
    .out0(decoder_3_out0[0]), .out1(decoder_3_out0[1]), .out2(decoder_3_out0[2]), .out3(decoder_3_out0[3]),
    .out4(decoder_3_out0[4]), .out5(decoder_3_out0[5]), .out6(decoder_3_out0[6]), .out7(decoder_3_out0[7]),
    .out8(decoder_3_out8[0]), .out9(decoder_3_out8[1]), .out10(decoder_3_out8[2]), .out11(decoder_3_out8[3]),
    .out12(decoder_3_out8[4]), .out13(decoder_3_out8[5]), .out14(decoder_3_out8[6]),
    .out15(decoder_3_out8[7]), .out16(decoder_3_out16[0]), .out17(decoder_3_out16[1]),
    .out18(decoder_3_out16[2]), .out19(decoder_3_out16[3]), .out20(decoder_3_out16[4]),
    .out21(decoder_3_out16[5]), .out22(decoder_3_out16[6]), .out23(decoder_3_out16[7]),
    .out24(decoder_3_out24[0]), .out25(decoder_3_out24[1]), .out26(decoder_3_out24[2]),
    .out27(decoder_3_out24[3]), .out28(decoder_3_out24[4]), .out29(decoder_3_out24[5]),
    .out30(decoder_3_out24[6]), .out31(decoder_3_out24[7]));  // open: sel, en
  Register #(.width(32)) x16 (.D(32'hdeadbeef), .en(decoder_1_out1[16]), .clk(clock_3_out), .Q(x16_q));  // open: clr
  Register #(.width(32)) x17 (.D(32'hdeadbeef), .en(decoder_1_out1[17]), .clk(clock_3_out), .Q(x17_q));  // open: clr
  Register #(.width(32)) x18 (.D(32'hdeadbeef), .en(decoder_1_out1[18]), .clk(clock_3_out), .Q(x18_q));  // open: clr
  Register #(.width(32)) x19 (.D(32'hdeadbeef), .en(decoder_1_out1[19]), .clk(clock_3_out), .Q(x19_q));  // open: clr
  Register #(.width(32)) x20 (.D(32'hdeadbeef), .en(decoder_1_out1[20]), .clk(clock_3_out), .Q(x20_q));  // open: clr
  Register #(.width(32)) x21 (.D(32'hdeadbeef), .en(decoder_1_out1[21]), .clk(clock_3_out), .Q(x21_q));  // open: clr
  Register #(.width(32)) x22 (.D(32'hdeadbeef), .en(decoder_1_out1[22]), .clk(clock_3_out), .Q(x22_q));  // open: clr
  Register #(.width(32)) x23 (.D(32'hdeadbeef), .en(decoder_1_out1[23]), .clk(clock_3_out), .Q(x23_q));  // open: clr
  Register #(.width(32)) x24 (.D(32'hdeadbeef), .en(decoder_1_out1[24]), .clk(clock_3_out), .Q(x24_q));  // open: clr
  Register #(.width(32)) x25 (.D(32'hdeadbeef), .en(decoder_1_out1[25]), .clk(clock_3_out), .Q(x25_q));  // open: clr
  Register #(.width(32)) x26 (.D(32'hdeadbeef), .en(decoder_1_out1[26]), .clk(clock_3_out), .Q(x26_q));  // open: clr
  Register #(.width(32)) x27 (.D(32'hdeadbeef), .en(decoder_1_out1[27]), .clk(clock_3_out), .Q(x27_q));  // open: clr
  Register #(.width(32)) x28 (.D(32'hdeadbeef), .en(decoder_1_out1[28]), .clk(clock_3_out), .Q(x28_q));  // open: clr
  Register #(.width(32)) x29 (.D(32'hdeadbeef), .en(decoder_1_out1[29]), .clk(clock_3_out), .Q(x29_q));  // open: clr
  Register #(.width(32)) x30 (.D(32'hdeadbeef), .en(decoder_1_out1[30]), .clk(clock_3_out), .Q(x30_q));  // open: clr
  Register #(.width(32)) x31 (.D(32'hdeadbeef), .en(decoder_1_out1[31]), .clk(clock_3_out), .Q(x31_q));  // open: clr

  // Other names for the same wires on the sheet: DRMUX[1:0] = in_4; LD_REG = in_3; PC[31:0] = out_5;
  //   PCMUX[1:0] = in_2; ResetSim = in_1

  // Notes on the sheet:
  //   DR
  //   SR1
  //   SR2
endmodule
